# Fritzing sketch DoButton (saved by Fritzing 0.7.9b)
breadboards: 2

parts:
  Arduino1 = Arduino
  S1 = Round Pushbutton
  LED1 = Red LED - 5mm [package="5 mm [THT]"]
  part = 10k Ω Resistor [package=THT]  # not connected
  R1 = 10k Ω Resistor [package=THT]
  part_2 = Screw terminal - 2 pins [package=THT]  # not connected

nets:
  GND: Arduino1.GND, LED1.cathode, R1.Pin_0
  N1: Arduino1.D5, LED1.anode
  N2: Arduino1.D2, S1.leg0, R1.Pin_1
  N3: Arduino1.+5V, S1.leg1
